# Fritzing sketch LCSmouse (saved by Fritzing 0.9.0b)

parts:
  Pro_Micro_-_5V/16MHz = Pro Micro
  Thumb_Joystick = Thumb Joystick

nets:
  N1: Pro_Micro_-_5V/16MHz.D15/SCLK, Thumb_Joystick.SEL
  N2: Pro_Micro_-_5V/16MHz.D18/A0, Thumb_Joystick.HORZ
  N3: Pro_Micro_-_5V/16MHz.D19/A1, Thumb_Joystick.VERT
  VCC: Pro_Micro_-_5V/16MHz.VCC, Thumb_Joystick.VCC
  GND: Pro_Micro_-_5V/16MHz.GND, Thumb_Joystick.GND

custom parts:
  Pro Micro: The SparkFun Pro Micro is a complete USB-based microcontoller development system, in a very small footprint, capable of implementing many types of projects. All programming can be done via the USB port.
