# Fritzing sketch LCSmouseBT (saved by Fritzing 0.9.0b)

parts:
  PowerBoost_500_Charger = PowerBoost 500 Charger
  Pro_Micro_-_5V/16MHz = Pro Micro
  Thumb_Joystick = Thumb Joystick
  Lithium_Ion_Polymer_Battery_500mAh = Polymer Lithium Ion Battery - Generic
  Roving_RN42-HID = Bluetooth Mate Silver
  Switch = SWITCH-DPDT [package=ayz0202]

nets (from the breadboard view):
  GND: PowerBoost_500_Charger.GND, Lithium_Ion_Polymer_Battery_500mAh.GND, Switch.2
  N1: PowerBoost_500_Charger.VBAT, Lithium_Ion_Polymer_Battery_500mAh.VCC
  N2: PowerBoost_500_Charger.ENABLE, Switch.3
  N3: PowerBoost_500_Charger.5.0V, Switch.5
  N4: Pro_Micro_-_5V/16MHz.TX1, Roving_RN42-HID.RX-I
  N5: Pro_Micro_-_5V/16MHz.RX0, Roving_RN42-HID.TX-O
  N6: Pro_Micro_-_5V/16MHz.GND#3, Roving_RN42-HID.GND
  N7: Pro_Micro_-_5V/16MHz.D15/SCLK, Thumb_Joystick.SEL
  N8: Pro_Micro_-_5V/16MHz.D18/A0, Thumb_Joystick.HORZ
  N9: Pro_Micro_-_5V/16MHz.D19/A1, Thumb_Joystick.VERT
  VCC: Pro_Micro_-_5V/16MHz.VCC, Thumb_Joystick.VCC, Roving_RN42-HID.VCC
  N10: Pro_Micro_-_5V/16MHz.GND#23, Thumb_Joystick.GND, Switch.1
  N11: Pro_Micro_-_5V/16MHz.RAW, Switch.6

custom parts:
  PowerBoost 500 Charger: The PowerBoost 500C is a little DC/DC boost converter module that can be powered by any 3.7V LiIon/LiPoly battery, and convert the battery output to 5.2V DC for running your 5V projects. At its heart is a TPS61090 boost converter from TI. This boost converter chip has some really nice extras such as low battery detection, 2A internal switch, synchronous conversion, excellent efficiency, and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
  Pro Micro: The SparkFun Pro Micro is a complete USB-based microcontoller development system, in a very small footprint, capable of implementing many types of projects. All programming can be done via the USB port.
  Polymer Lithium Ion Battery - Generic: Description: These are batteries based on the new Polymer Lithium Ion chemistry. This is the highest energy density currently in production. Comes terminated with a standard 2-pin JST-PH connector - 2mm spacing between pins. These batteries require special charging. Do not attempt to charge these with anything but a specialized LiPo charger. Battery includes built-in protection against over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
  Bluetooth Mate Silver: Description: The Bluetooth Mate is very similar to our BlueSMiRF modem, but it is designed specifically to be used with our Arduino Pros and LilyPad Arduinos. These modems work as a serial (RX/TX) pipe, and are a great wireless replacement for serial cables. Any serial stream from 9600 to 115200bps can be passed seamlessly from your computer to your target. Bluetooth Mate has the same pin out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
